# Fritzing sketch greenhouse_schematic (saved by Fritzing 0.9.3b)
breadboards: 1

parts:
  RHT1 = Humidity and Temperature Sensor RHT03
  LDR = Photocell (LDR) [package=THT]
  R2 = Resistor [tolerance=±5% resistance=1k package="2010 [SMD]"]
  Part2 = Soil Moisture Sensor
  Water_Level_Sensor1 = Water Level Sensor
  color_sensor = TCS230 Color Sensor [part_number=101209]
  U1 = RELAY [package=relay-jzc]
  M1 = DC Motor
  U2 = RELAY [package=relay-jzc]
  Part1 = Arduino Uno (Rev3)

nets:
  VCC: RHT1.Vcc, LDR.pin_0, Part2.VCC, Water_Level_Sensor1.VCC, color_sensor.Vcc, Part1.5V
  N1: RHT1.Data-signal, Part1.D9_PWM
  GND: RHT1.GND_1, R2.Pin_1, Part2.GND, Water_Level_Sensor1.GND, color_sensor.Gnd, U1.COIL2, M1.pin_1, U2.COIL2, Part1.GND
  N2: LDR.pin_1, R2.Pin_0, Part1.A0
  N3: Part2.SIG, Part1.A1
  N4: Water_Level_Sensor1.SIG, Part1.A2
  N5: color_sensor.OE, Part1.D3_PWM
  N6: color_sensor.S3, Part1.D8
  N7: color_sensor.S2, Part1.D7
  N8: U1.NO, M1.pin_2
  N9: U1.COIL1, Part1.D2
  N10: U2.COIL1, Part1.D5_PWM

custom parts:
  Water Level Sensor: A water level sensor. This sensor operates at 3V to 5V. The Sig (signal) pin outputs an analogue signal that is in proportion to the amount of water in contact with the sensor.
  TCS230 Color Sensor: TCS230
